// Digital circuit flipflopRS.dig as structural Verilog
module flipflopRS (
  input  in_2,
  input  in_3,
  output Output
);

  wire nor_2_out;

  nor nor_1 (Output, in_2, nor_2_out);
  nor nor_2 (nor_2_out, Output, in_3);

  // Notes on the sheet:
  //   R
  //   S
  //   El flip-flop RS tiene 4 estados, 
  //   R S
  //   0 0 -> Memoria, guarda el último dato que se haya puesto en la salida.
  //   como siempre hay una compuerta que da salida, se mantiene el estado
  //   1 0 -> Resetea, manda el estado de la salida a 0.
  //   como R se activa, la compuerta N1 da una salida 0
  //   0 1 -> Setea, permite ajustar el valor que se tendrá en la salida.
  //   se activa S entonces la compuerta N2 manda una señal de 0 a la
  //   N1, lo que hace que salida = 1 
  //   1 1 -> Comportamiento que no se puede predecir, no se recomienda
endmodule
